# Fritzing sketch sd_card_wiring (saved by Fritzing 0.9.4)

parts:
  Part1 = Photon
  U1 = microSD Socket [package=usd-socket-pp]  # not connected
  J3 = screw terminal, 7 pins

nets:
  N1: Part1.A1, J3.pin6
  N2: Part1.A2, J3.pin2
  N3: Part1.A3, J3.pin4
  N4: Part1.A4, J3.pin5
  N5: Part1.A5, J3.pin3
  N6: Part1.VIN, J3.pin1
  N7: Part1.GND, J3.pin7

notes:
  VCC
  CS
  DI
  DO
  SCK
  CD
  GND
